// Logisim project P4.circ as structural Verilog: 15 circuits, main circuit main
module main (
  input  [3:0] in_1,
  input  [3:0] in_2,
  input  [3:0] in_3,
  input  [3:0] in_4,
  input  [3:0] in_5
);

  wire CLK, keyboard_1_avail, keyboard_2_avail, keyboarddriver_1_read, keyboarddriver_2_read,
       pull_resistor_1_node, ttydriver_1_write, ttydriver_2_write, ttydriver_3_write, vpwbmonitor_1_last_fe;
  wire [3:0] vpwbmonitor_1_last_addr;
  wire [6:0] keyboard_1_data, keyboard_2_data, ttydriver_1_data, ttydriver_2_data, ttydriver_3_data;
  wire [7:0] vpwbmonitor_1_last_data;
  wire [24:0] vpwbmonitor_1_out_4;
  wire [31:0] vpwbmonitor_1_out_3;

  Clock clock_1 (.out(CLK));
  Keyboard keyboard_1 (
    .clk(CLK), .re(keyboarddriver_1_read), .avail(keyboard_1_avail), .data(keyboard_1_data));  // open: clr
  Keyboard keyboard_2 (
    .clk(CLK), .re(keyboarddriver_2_read), .avail(keyboard_2_avail), .data(keyboard_2_data));  // open: clr
  Pull_Resistor #(.pull(1)) pull_resistor_1 (.node(pull_resistor_1_node));
  KeyboardDriver keyboarddriver_1 (
    .DATA(keyboard_1_data), .DEST(in_1), .DR(keyboard_1_avail), .CLK(CLK), .RXIN(pull_resistor_1_node),
    .READ(keyboarddriver_1_read), .TXOUT(pull_resistor_1_node));
  KeyboardDriver keyboarddriver_2 (
    .DATA(keyboard_2_data), .DEST(in_3), .DR(keyboard_2_avail), .CLK(CLK), .RXIN(pull_resistor_1_node),
    .READ(keyboarddriver_2_read), .TXOUT(pull_resistor_1_node));
  // Probe on vpwbmonitor_1_out_3
  VPWBMonitor vpwbmonitor_1 (
    .RXIN(pull_resistor_1_node), .CLK(CLK), .LAST_FE(vpwbmonitor_1_last_fe),
    .LAST_ADDR(vpwbmonitor_1_last_addr), .LAST_DATA(vpwbmonitor_1_last_data), .out_3(vpwbmonitor_1_out_3),
    .out_4(vpwbmonitor_1_out_4));
  TTY tty_1 (.data(ttydriver_1_data), .clk(CLK), .we(ttydriver_1_write));  // open: clr
  TTYDriver ttydriver_1 (
    .RXIN(pull_resistor_1_node), .CLK(CLK), .TTY_ADDR(in_2), .TXOUT(pull_resistor_1_node),
    .WRITE(ttydriver_1_write), .DATA(ttydriver_1_data));
  TTY tty_2 (.data(ttydriver_2_data), .clk(CLK), .we(ttydriver_2_write));  // open: clr
  TTYDriver ttydriver_2 (
    .RXIN(pull_resistor_1_node), .CLK(CLK), .TTY_ADDR(in_4), .TXOUT(pull_resistor_1_node),
    .WRITE(ttydriver_2_write), .DATA(ttydriver_2_data));
  TTY tty_3 (.data(ttydriver_3_data), .clk(CLK), .we(ttydriver_3_write));  // open: clr
  TTYDriver ttydriver_3 (
    .RXIN(pull_resistor_1_node), .CLK(CLK), .TTY_ADDR(in_5), .TXOUT(pull_resistor_1_node),
    .WRITE(ttydriver_3_write), .DATA(ttydriver_3_data));
  // Probe on vpwbmonitor_1_out_4
  // Probe on vpwbmonitor_1_last_fe
  // Probe on vpwbmonitor_1_last_addr
  // Probe on vpwbmonitor_1_last_data
endmodule

module KeyboardDriver (
  input  DR,
  input  [6:0] DATA,
  input  RXIN,
  input  [3:0] DEST,
  input  CLK,
  output TXOUT,
  output READ
);

  wire ADDR, and_1_out, CHKDR, CS, JUMP, O, or_1_out, txrxd_1_din, vpwbcontroller_1_ser_out, W;
  wire [5:5] rom_1_data;
  wire [7:0] NPC, PC, PCPLUS1, PCTARGET;
  wire [11:0] multiplexer_1_out;

  Register register_1 (.D(NPC), .en(1'b1), .clk(CLK), .Q(PC));  // open: clr
  Adder adder_1 (.a(8'h1), .b(PC), .out(PCPLUS1));  // open: cin, cout
  ROM #(.dataWidth(16)) rom_1 (.addr(PC), .data({PCTARGET, JUMP, CHKDR, rom_1_data[5], READ, ADDR, O, W, CS}));
  Multiplexer #(.width(12)) multiplexer_1 (.in0(12'h1), .in1({DEST, 1'b0, DATA}), .out(multiplexer_1_out), .sel(ADDR));
  VPWBController vpwbcontroller_1 (
    .O(O), .ADDR(ADDR), .DATAIN(multiplexer_1_out), .CS(CS), .W(W), .CLK(CLK), .SER_IN(txrxd_1_din),
    .SER_OUT(vpwbcontroller_1_ser_out));  // open: I, DATAOUT
  and and_1 (and_1_out, CHKDR, DR);
  or or_1 (or_1_out, and_1_out, JUMP);
  Multiplexer #(.width(8)) multiplexer_2 (.in0(PCPLUS1), .in1(PCTARGET), .out(NPC), .sel(or_1_out));
  TXRXD txrxd_1 (.DOUT(vpwbcontroller_1_ser_out), .RXIN(RXIN), .DIN(txrxd_1_din), .TXOUT(TXOUT));

  // Other names for the same wires on the sheet: DATA_t[6:0] = DATA

  // Notes on the sheet:
  //   contents of rom_1 (hex, n*v repeats v):
  //   7 4 7 547 387 1c 387
endmodule

module TTYDriver (
  input  RXIN,
  input  [3:0] TTY_ADDR,
  input  CLK,
  output [6:0] DATA,
  output TXOUT,
  output WRITE
);

  wire ADDR, and_1_out, CHKDR, comparator_1_eq, CS, DR, JUMP, not_1_out, O, or_1_out, txrxd_1_din,
       vpwbcontroller_1_ser_out, W, WRITE_TTY;
  wire [5:5] rom_1_data;
  wire [7:0] NPC, PC, PCPLUS1, PCTARGET;
  wire [11:0] DATAOUT, register_2_q;

  Register register_1 (.D(NPC), .en(1'b1), .clk(CLK), .Q(PC));  // open: clr
  Adder adder_1 (.a(8'h1), .b(PC), .out(PCPLUS1));  // open: cin, cout
  ROM #(.dataWidth(16)) rom_1 (.addr(PC), .data({PCTARGET, JUMP, CHKDR, rom_1_data[5], WRITE_TTY, ADDR, O, W, CS}));
  Register #(.width(12)) register_2 (
    .D(DATAOUT), .en(not_1_out), .clk(CLK), .Q({register_2_q[11:2], DR, register_2_q[0]}));  // open: clr
  not not_1 (not_1_out, O);
  and and_1 (and_1_out, CHKDR, DR);
  VPWBController vpwbcontroller_1 (
    .O(O), .ADDR(ADDR), .DATAIN({4'b1111, TTY_ADDR, 4'b0001}), .CS(CS), .W(W), .CLK(CLK),
    .SER_IN(txrxd_1_din), .DATAOUT(DATAOUT), .SER_OUT(vpwbcontroller_1_ser_out));  // open: I
  Multiplexer #(.width(8)) multiplexer_1 (.in0(PCPLUS1), .in1(PCTARGET), .out(NPC), .sel(or_1_out));
  or or_1 (or_1_out, and_1_out, JUMP);
  Comparator #(.mode("unsigned"), .width(4)) comparator_1 (
    .a(register_2_q[11:8]), .b(TTY_ADDR), .eq(comparator_1_eq));  // open: gt, lt
  and and_2 (WRITE, comparator_1_eq, WRITE_TTY);
  Multiplexer #(.width(7)) multiplexer_2 (
    .in0({7{1'b0}}), .in1({register_2_q[6:2], DR, register_2_q[0]}), .out(DATA), .sel(WRITE));
  TXRXD txrxd_1 (.DOUT(vpwbcontroller_1_ser_out), .RXIN(RXIN), .DIN(txrxd_1_din), .TXOUT(TXOUT));

  // Other names for the same wires on the sheet: CHAR[6:0] = DATA

  // Notes on the sheet:
  //   contents of rom_1 (hex, n*v repeats v):
  //   7 4 7 2 647 87 a 17 87
endmodule

module VPWBMonitor (
  input  RXIN,
  input  CLK,
  output [31:0] out_3,
  output [24:0] out_4,
  output LAST_FE,
  output [3:0] LAST_ADDR,
  output [7:0] LAST_DATA
);

  wire B0_ERR, B1_ERR, B2_ERR, B3_ERR, B4_ERR, B5_ERR, B6_ERR, B7_ERR, B8_ERR, B9_ERR, BA_ERR, BB_ERR,
       FOUND_IDLE, I4, I5, I6, I7, I8, I9, I10, I11, I12, I13, I14, I15, I16, I17, I18, I19, I20, I21, I22,
       I23, I24, I25, I26, I27, I28, I29, NEW_IDLE, not_7_out;
  wire [0:0] not_1_out, not_2_out, not_9_out, not_10_out, not_15_out, not_16_out, shifter_1_out_3,
       shifter_2_out_3, shifter_3_out_3, shifter_6_out_3, shifter_7_out_3, shifter_8_out_3, shifter_10_out_3,
       shifter_11_out_3, shifter_12_out_3;
  wire [1:0] shifter_1_out, shifter_2_out, shifter_3_out, shifter_6_out, shifter_7_out, shifter_8_out,
       shifter_10_out, shifter_11_out, shifter_12_out;
  wire [4:0] FRAME_LENGTH, priority_encoder_1_out;
  wire [5:0] subtractor_1_out, subtractor_2_out;
  wire [9:0] shifter_12_out_2;
  wire [10:0] shifter_11_out_2;
  wire [11:0] shifter_10_out_2, shifter_13_out;
  wire [13:0] shifter_8_out_2;
  wire [14:0] shifter_7_out_2;
  wire [15:0] shifter_6_out_2, shifter_9_out;
  wire [17:0] shifter_3_out_2;
  wire [18:0] shifter_2_out_2;
  wire [19:0] shifter_1_out_2, shifter_4_out;
  wire [24:0] and_6_out, not_8_out;
  wire [25:0] shifter_5_out;

  not not_1 (not_1_out[0], LAST_DATA[1]);
  not not_2 (not_2_out[0], LAST_DATA[3]);
  Subtractor #(.width(6)) subtractor_1 (
    .a(6'b011001), .b({1'b0, FRAME_LENGTH}), .out(subtractor_1_out));  // open: bin, bout
  Shifter #(.shift("lr"), .width(23)) shifter_1 (
    .in(out_4[24:2]), .\dist ({4'b0000, LAST_DATA[0]}),
    .out({shifter_1_out_2, shifter_1_out, shifter_1_out_3[0]}));
  Shifter #(.shift("lr"), .width(22)) shifter_2 (
    .in({shifter_1_out_2, shifter_1_out}), .\dist ({4'b0000, not_1_out[0]}),
    .out({shifter_2_out_2, shifter_2_out, shifter_2_out_3[0]}));
  Shifter #(.shift("lr"), .width(21)) shifter_3 (
    .in({shifter_2_out_2, shifter_2_out}), .\dist ({4'b0000, LAST_DATA[2]}),
    .out({shifter_3_out_2, shifter_3_out, shifter_3_out_3[0]}));
  Shifter #(.shift("lr"), .width(20)) shifter_4 (
    .in({shifter_3_out_2, shifter_3_out}), .\dist ({4'b0000, not_2_out[0]}), .out(shifter_4_out));
  // Probe on shifter_5_out
  and and_1 (B0_ERR, ~out_4[1], ~out_4[2], ~out_4[3]);  // AND_Gate
  not not_3 (LAST_DATA[0], out_4[2]);
  and and_2 (B1_ERR, shifter_1_out_3[0], shifter_1_out[0], shifter_1_out[1]);
  not not_4 (LAST_DATA[1], shifter_1_out[0]);
  and and_3 (B2_ERR, ~shifter_2_out_3[0], ~shifter_2_out[0], ~shifter_2_out[1]);  // AND_Gate
  not not_5 (LAST_DATA[2], shifter_2_out[0]);
  and and_4 (B3_ERR, shifter_3_out_3[0], shifter_3_out[0], shifter_3_out[1]);
  not not_6 (LAST_DATA[3], shifter_3_out[0]);
  not not_7 (not_7_out, RXIN);
  Shift_Register #(.length(32)) shift_register_1 (
    .shift(1'b1), .in(not_7_out), .clk(CLK), .out(out_3[31]), .q0(out_3[0]), .q1(out_3[1]), .q2(out_3[2]),
    .q3(out_3[3]), .q4(out_3[4]), .q5(out_3[5]), .q6(out_3[6]), .q7(out_3[7]), .q8(out_3[8]), .q9(out_3[9]),
    .q10(out_3[10]), .q11(out_3[11]), .q12(out_3[12]), .q13(out_3[13]), .q14(out_3[14]), .q15(out_3[15]),
    .q16(out_3[16]), .q17(out_3[17]), .q18(out_3[18]), .q19(out_3[19]), .q20(out_3[20]), .q21(out_3[21]),
    .q22(out_3[22]), .q23(out_3[23]), .q24(out_3[24]), .q25(out_3[25]), .q26(out_3[26]), .q27(out_3[27]),
    .q28(out_3[28]), .q29(out_3[29]), .q30(out_3[30]));  // open: load, clr, d0, d1, d2, d3, d4, d5, d6, d7, d8, d9, d10, d11, d12, d13, d14, d15, d16, d17, d18, d19, d20, d21, d22, d23, d24, d25, d26, d27, d28, d29, d30, d31, q31
  and and_5 (NEW_IDLE, ~out_3[0], ~out_3[1], ~out_3[2], out_3[3]);  // AND_Gate
  assign not_8_out = ~shifter_5_out[24:0];  // NOT_Gate not_8, 25 bits wide
  Shifter #(.shift("ar"), .width(26)) shifter_5 (.in(26'h2000000), .\dist (subtractor_1_out[4:0]), .out(shifter_5_out));
  not not_9 (not_9_out[0], LAST_DATA[5]);
  not not_10 (not_10_out[0], LAST_DATA[7]);
  Shifter #(.shift("lr"), .width(19)) shifter_6 (
    .in(shifter_4_out[19:1]), .\dist ({4'b0000, LAST_DATA[4]}),
    .out({shifter_6_out_2, shifter_6_out, shifter_6_out_3[0]}));
  Shifter #(.shift("lr"), .width(18)) shifter_7 (
    .in({shifter_6_out_2, shifter_6_out}), .\dist ({4'b0000, not_9_out[0]}),
    .out({shifter_7_out_2, shifter_7_out, shifter_7_out_3[0]}));
  Shifter #(.shift("lr"), .width(17)) shifter_8 (
    .in({shifter_7_out_2, shifter_7_out}), .\dist ({4'b0000, LAST_DATA[6]}),
    .out({shifter_8_out_2, shifter_8_out, shifter_8_out_3[0]}));
  Shifter #(.shift("lr"), .width(16)) shifter_9 (
    .in({shifter_8_out_2, shifter_8_out}), .\dist ({3'b000, not_10_out[0]}), .out(shifter_9_out));
  // Probe on and_6_out
  Register #(.width(25)) register_1 (.D(and_6_out), .en(NEW_IDLE), .clk(CLK), .Q(out_4));  // open: clr
  assign and_6_out = out_3[27:3] & not_8_out;  // AND_Gate and_6, 25 bits wide
  and and_7 (B4_ERR, ~shifter_4_out[0], ~shifter_4_out[1], ~shifter_4_out[2]);  // AND_Gate
  not not_11 (LAST_DATA[4], shifter_4_out[1]);
  and and_8 (B5_ERR, shifter_6_out_3[0], shifter_6_out[0], shifter_6_out[1]);
  not not_12 (LAST_DATA[5], shifter_6_out[0]);
  and and_9 (B6_ERR, ~shifter_7_out_3[0], ~shifter_7_out[0], ~shifter_7_out[1]);  // AND_Gate
  not not_13 (LAST_DATA[6], shifter_7_out[0]);
  and and_10 (B7_ERR, shifter_8_out_3[0], shifter_8_out[0], shifter_8_out[1]);
  not not_14 (LAST_DATA[7], shifter_8_out[0]);
  not not_15 (not_15_out[0], LAST_ADDR[1]);
  not not_16 (not_16_out[0], LAST_ADDR[3]);
  and and_11 (B8_ERR, ~shifter_9_out[0], ~shifter_9_out[1], ~shifter_9_out[2]);  // AND_Gate
  not not_17 (LAST_ADDR[0], shifter_9_out[1]);
  Shifter #(.shift("lr"), .width(15)) shifter_10 (
    .in(shifter_9_out[15:1]), .\dist ({3'b000, LAST_ADDR[0]}),
    .out({shifter_10_out_2, shifter_10_out, shifter_10_out_3[0]}));
  and and_12 (B9_ERR, shifter_10_out_3[0], shifter_10_out[0], shifter_10_out[1]);
  not not_18 (LAST_ADDR[1], shifter_10_out[0]);
  Shifter #(.shift("lr"), .width(14)) shifter_11 (
    .in({shifter_10_out_2, shifter_10_out}), .\dist ({3'b000, not_15_out[0]}),
    .out({shifter_11_out_2, shifter_11_out, shifter_11_out_3[0]}));
  and and_13 (BA_ERR, ~shifter_11_out_3[0], ~shifter_11_out[0], ~shifter_11_out[1]);  // AND_Gate
  not not_19 (LAST_ADDR[2], shifter_11_out[0]);
  Shifter #(.shift("lr"), .width(13)) shifter_12 (
    .in({shifter_11_out_2, shifter_11_out}), .\dist ({3'b000, LAST_ADDR[2]}),
    .out({shifter_12_out_2, shifter_12_out, shifter_12_out_3[0]}));
  and and_14 (BB_ERR, shifter_12_out_3[0], shifter_12_out[0], shifter_12_out[1]);
  not not_20 (LAST_ADDR[3], shifter_12_out[0]);
  Shifter #(.shift("lr"), .width(12)) shifter_13 (
    .in({shifter_12_out_2, shifter_12_out}), .\dist ({3'b000, not_16_out[0]}), .out(shifter_13_out));
  and and_15 (I29, ~out_3[31], ~out_3[30], ~out_3[29]);  // AND_Gate
  and and_16 (I28, ~out_3[30], ~out_3[29], ~out_3[28]);  // AND_Gate
  and and_17 (I27, ~out_3[29], ~out_3[28], ~out_3[27]);  // AND_Gate
  and and_18 (I26, ~out_3[28], ~out_3[27], ~out_3[26]);  // AND_Gate
  and and_19 (I24, ~out_3[26], ~out_3[25], ~out_3[24]);  // AND_Gate
  and and_20 (I23, ~out_3[25], ~out_3[24], ~out_3[23]);  // AND_Gate
  and and_21 (I25, ~out_3[27], ~out_3[26], ~out_3[25]);  // AND_Gate
  or or_1 (LAST_FE, out_4[1], B0_ERR, B1_ERR, B2_ERR, B3_ERR, B4_ERR, B5_ERR, B6_ERR, B7_ERR, B8_ERR, B9_ERR, BA_ERR, BB_ERR);
  and and_22 (I22, ~out_3[24], ~out_3[23], ~out_3[22]);  // AND_Gate
  and and_23 (I21, ~out_3[23], ~out_3[22], ~out_3[21]);  // AND_Gate
  and and_24 (I20, ~out_3[22], ~out_3[21], ~out_3[20]);  // AND_Gate
  and and_25 (I19, ~out_3[21], ~out_3[20], ~out_3[19]);  // AND_Gate
  and and_26 (I18, ~out_3[20], ~out_3[19], ~out_3[18]);  // AND_Gate
  and and_27 (I17, ~out_3[19], ~out_3[18], ~out_3[17]);  // AND_Gate
  and and_28 (I16, ~out_3[18], ~out_3[17], ~out_3[16]);  // AND_Gate
  and and_29 (I15, ~out_3[17], ~out_3[16], ~out_3[15]);  // AND_Gate
  and and_30 (I14, ~out_3[16], ~out_3[15], ~out_3[14]);  // AND_Gate
  and and_31 (I13, ~out_3[15], ~out_3[14], ~out_3[13]);  // AND_Gate
  and and_32 (I12, ~out_3[14], ~out_3[13], ~out_3[12]);  // AND_Gate
  and and_33 (I11, ~out_3[13], ~out_3[12], ~out_3[11]);  // AND_Gate
  and and_34 (I10, ~out_3[12], ~out_3[11], ~out_3[10]);  // AND_Gate
  and and_35 (I9, ~out_3[11], ~out_3[10], ~out_3[9]);  // AND_Gate
  and and_36 (I8, ~out_3[10], ~out_3[9], ~out_3[8]);  // AND_Gate
  and and_37 (I7, ~out_3[9], ~out_3[8], ~out_3[7]);  // AND_Gate
  and and_38 (I6, ~out_3[8], ~out_3[7], ~out_3[6]);  // AND_Gate
  and and_39 (I5, ~out_3[7], ~out_3[6], ~out_3[5]);  // AND_Gate
  and and_40 (I4, ~out_3[6], ~out_3[5], ~out_3[4]);  // AND_Gate
  Priority_Encoder #(.select(5)) priority_encoder_1 (
    .in0(I29), .in1(I28), .in2(I27), .in3(I26), .in4(I25), .in5(I24), .in6(I23), .in7(I22), .in8(I21),
    .in9(I20), .in10(I19), .in11(I18), .in12(I17), .in13(I16), .in14(I15), .in15(I14), .in16(I13),
    .in17(I12), .in18(I11), .in19(I10), .in20(I9), .in21(I8), .in22(I7), .in23(I6), .in24(I5), .in25(I4),
    .in26(1'b0), .in27(1'b0), .in28(1'b0), .in29(1'b0), .in30(1'b0), .in31(1'b0),
    .out(priority_encoder_1_out), .gs(FOUND_IDLE));  // open: en_out, en_in
  Subtractor #(.width(6)) subtractor_2 (
    .a(6'b011010), .b({1'b0, priority_encoder_1_out}), .out(subtractor_2_out));  // open: bin, bout
  Multiplexer #(.width(5)) multiplexer_1 (
    .in0({5{1'b0}}), .in1(subtractor_2_out[4:0]), .out(FRAME_LENGTH), .sel(FOUND_IDLE));

  // Other names for the same wires on the sheet: LAST_FRAME[24:0] = out_4; HIST[31:0] = out_3; B8 = LAST_ADDR[0];
  //   B9 = LAST_ADDR[1]; BA = LAST_ADDR[2]; BB = LAST_ADDR[3]; B0 = LAST_DATA[0]; B1 = LAST_DATA[1];
  //   B2 = LAST_DATA[2]; B3 = LAST_DATA[3]; B4 = LAST_DATA[4]; B5 = LAST_DATA[5]; B6 = LAST_DATA[6];
  //   B7 = LAST_DATA[7]; EOF_ERR = out_4[1]
endmodule

module TXRXD (
  input  DOUT,
  input  RXIN,
  output TXOUT,
  output DIN
);

  assign TXOUT = DOUT ? ~DOUT : 1'bz;  // Controlled_Inverter controlled_inverter_1
  not not_1 (DIN, RXIN);

  // Notes on the sheet:
  //   TXOUT: pull=down
endmodule

module VPWBController (
  input  CS,
  input  W,
  input  SER_IN,
  input  O,
  input  ADDR,
  input  [11:0] DATAIN,
  input  CLK,
  output SER_OUT,
  output I,
  output [11:0] DATAOUT
);

  wire Full, not_1_out, not_2_out, READNOTEMPTY, register_1_p1, undriven, vpwbrx_1_empty;

  // Register #(.width(12)) register_1: pin names not known; wires that end beside it: register_1_p1, register_1_p1
  not not_1 (not_1_out, CS);
  VPWBTX vpwbtx_1 (
    .FRAME_IN(DATAIN), .WRITE(W), .ENA(not_1_out), .CLK(CLK), .SER_IN(SER_IN), .SER_OUT(SER_OUT));  // open: FULL, IDLE
  not not_2 (not_2_out, CS);
  not not_3 (READNOTEMPTY, vpwbrx_1_empty);
  VPWBRX vpwbrx_1 (
    .READ(O), .ENA(not_2_out), .CLK(CLK), .SER_IN(SER_OUT), .FRAME_OUT(DATAOUT), .FULL(Full),
    .EMPTY(vpwbrx_1_empty));  // open: CARE, ADDR
  Multiplexer multiplexer_1 (.in0(undriven), .sel(ADDR));  // open: in1, out
endmodule

module VPWBTX (
  input  [11:0] FRAME_IN,
  input  SER_IN,
  input  WRITE,
  input  ENA,
  input  CLK,
  output SER_OUT,
  output FULL,
  output IDLE
);

  wire and_1_out, and_2_out, and_4_out, not_1_out, not_2_out, vpwbarbiter_1_arbl, vpwbarbiter_1_bitcmp,
       vpwbframequeue_1_empty, vpwbobserver_1_idle, vpwbsro_1_empty, vpwbsro_1_ser_out;
  wire [3:0] vpwbsro_1_bitsleft;
  wire [11:0] vpwbframequeue_1_frame_out;

  not not_1 (not_1_out, vpwbsro_1_empty);
  not not_2 (not_2_out, vpwbframequeue_1_empty);
  and and_1 (and_1_out, not_2_out, vpwbsro_1_empty);
  VPWBFrameQueue vpwbframequeue_1 (
    .FRAME_IN(FRAME_IN), .ENQUEUE(WRITE), .ENA(ENA), .CLK(CLK), .DEQUEUE(and_1_out), .FULL(FULL),
    .FRAME_OUT(vpwbframequeue_1_frame_out), .EMPTY(vpwbframequeue_1_empty));
  VPWBSRO vpwbsro_1 (
    .LOAD(and_1_out), .ENA(ENA), .PARA_IN(vpwbframequeue_1_frame_out), .CLK(CLK), .SHIFT(and_4_out),
    .RELOAD(and_2_out), .EMPTY(vpwbsro_1_empty), .SER_OUT(vpwbsro_1_ser_out), .BITSLEFT(vpwbsro_1_bitsleft));
  // Probe on vpwbframequeue_1_frame_out
  and and_2 (and_2_out, vpwbarbiter_1_arbl, vpwbobserver_1_idle);
  and and_3 (IDLE, vpwbframequeue_1_empty, vpwbsro_1_empty);
  and and_4 (and_4_out, vpwbarbiter_1_bitcmp, not_1_out);
  VPWBArbiter vpwbarbiter_1 (
    .DW(not_1_out), .EVENBIT(vpwbsro_1_bitsleft[0]), .DOUT(vpwbsro_1_ser_out), .ENA(ENA), .CLK(CLK),
    .RX(SER_IN), .ARBL(vpwbarbiter_1_arbl), .BITCMP(vpwbarbiter_1_bitcmp), .TX(SER_OUT));
  VPWBObserver vpwbobserver_1 (.ENA(ENA), .CLK(CLK), .RX(SER_IN), .IDLE(vpwbobserver_1_idle));  // open: DIN, NEWBIT
endmodule

module VPWBRX (
  input  [3:0] CARE,
  input  [3:0] ADDR,
  input  SER_IN,
  input  READ,
  input  ENA,
  input  CLK,
  output [11:0] FRAME_OUT,
  output FULL,
  output EMPTY
);

  wire not_1_out, vpwbobserver_1_din, vpwbobserver_1_newbit, vpwbsri_1_full;
  wire [11:0] vpwbsri_1_para_out;

  not not_1 (not_1_out, vpwbsri_1_full);
  VPWBSRI vpwbsri_1 (
    .READ(not_1_out), .ENA(ENA), .CLK(CLK), .SER_IN(vpwbobserver_1_din), .NEWBIT(vpwbobserver_1_newbit),
    .FULL(vpwbsri_1_full), .PARA_OUT(vpwbsri_1_para_out));  // open: CLEAR
  VPWBFrameQueue vpwbframequeue_1 (
    .FRAME_IN(vpwbsri_1_para_out), .ENQUEUE(vpwbsri_1_full), .ENA(ENA), .CLK(CLK), .DEQUEUE(READ),
    .FULL(FULL), .FRAME_OUT(FRAME_OUT), .EMPTY(EMPTY));
  VPWBObserver vpwbobserver_1 (
    .ENA(ENA), .CLK(CLK), .RX(SER_IN), .DIN(vpwbobserver_1_din), .NEWBIT(vpwbobserver_1_newbit));  // open: IDLE
endmodule

module VPWBFrameQueue (
  input  [11:0] FRAME_IN,
  input  ENQUEUE,
  input  DEQUEUE,
  input  ENA,
  input  CLK,
  output [11:0] FRAME_OUT,
  output FULL,
  output EMPTY
);

  wire and_2_out, and_3_out, canENQUEUE, not_1_out, not_2_out, not_3_out, not_4_out, not_5_out, not_6_out,
       not_7_out, not_8_out, not_9_out, or_1_out, trueEMPTY, trueFULL, undriven, undriven_3;
  wire [2:0] CurrentIndex;
  wire [11:0] register_1_q, register_2_q, register_3_q, register_4_q, trueFRAME_OUT, undriven_2;

  not not_1 (not_1_out, FULL);
  not not_2 (not_2_out, DEQUEUE);
  Register #(.width(12)) register_1 (.D(FRAME_IN), .en(canENQUEUE), .clk(CLK), .Q(register_1_q), .clr(not_3_out));
  and and_1 (canENQUEUE, ENQUEUE, not_1_out, not_2_out);
  not not_3 (not_3_out, ENA);
  Register #(.width(12)) register_2 (.D(register_1_q), .en(canENQUEUE), .clk(CLK), .Q(register_2_q), .clr(not_4_out));
  not not_4 (not_4_out, ENA);
  Register #(.width(12)) register_3 (.D(register_2_q), .en(canENQUEUE), .clk(CLK), .Q(register_3_q), .clr(not_5_out));
  not not_5 (not_5_out, ENA);
  or or_1 (or_1_out, canENQUEUE, DEQUEUE);
  and and_2 (and_2_out, or_1_out, not_6_out);
  and and_3 (and_3_out, trueEMPTY, DEQUEUE);
  not not_6 (not_6_out, and_3_out);
  Register #(.width(12)) register_4 (.D(register_3_q), .en(canENQUEUE), .clk(CLK), .Q(register_4_q), .clr(not_7_out));
  not not_7 (not_7_out, ENA);
  not not_8 (not_8_out, DEQUEUE);
  Counter #(.max('h4), .width(3)) counter_1 (
    .count(and_2_out), .Q(CurrentIndex), .up(not_8_out), .clk(CLK), .clr(not_9_out));  // open: load, D, carry
  not not_9 (not_9_out, ENA);
  Comparator #(.width(3)) comparator_1 (.a(CurrentIndex), .b(3'b000), .eq(trueEMPTY));  // open: gt, lt
  Comparator #(.width(3)) comparator_2 (.a(CurrentIndex), .b(3'b100), .eq(trueFULL));  // open: gt, lt
  Multiplexer #(.select(3), .width(12)) multiplexer_1 (
    .in0({12{1'b0}}), .in1(register_1_q), .in2(register_2_q), .in3(register_3_q), .in4(register_4_q),
    .out(trueFRAME_OUT), .sel(CurrentIndex));  // open: in5, in6, in7
  Multiplexer multiplexer_2 (.in0(undriven), .in1(trueFULL), .out(FULL), .sel(ENA));
  Multiplexer #(.width(12)) multiplexer_3 (.in0(undriven_2), .in1(trueFRAME_OUT), .out(FRAME_OUT), .sel(ENA));
  Multiplexer multiplexer_4 (.in0(undriven_3), .in1(trueEMPTY), .out(EMPTY), .sel(ENA));
endmodule

module VPWBSRI (
  input  READ,
  input  SER_IN,
  input  NEWBIT,
  input  CLEAR,
  input  ENA,
  input  CLK,
  output FULL,
  output [11:0] PARA_OUT
);

  wire and_1_out, not_1_out, not_2_out, not_3_out, not_4_out, not_5_out, not_6_out, not_7_out, not_8_out,
       not_9_out, not_10_out, not_11_out, not_12_out, not_13_out, or_1_out, or_2_out, or_3_out, or_4_out,
       or_5_out, or_6_out, or_7_out, or_8_out, or_9_out, or_10_out, or_11_out, or_12_out, or_13_out;
  wire [11:0] register_1_q;

  Register #(.width(1)) register_1 (.D(SER_IN), .en(NEWBIT), .clk(CLK), .Q(register_1_q[0]), .clr(or_1_out));
  or or_1 (or_1_out, not_1_out, CLEAR);
  not not_1 (not_1_out, ENA);
  Register #(.width(1)) register_2 (.D(register_1_q[0]), .en(NEWBIT), .clk(CLK), .Q(register_1_q[1]), .clr(or_2_out));
  or or_2 (or_2_out, not_2_out, CLEAR);
  not not_2 (not_2_out, ENA);
  Register #(.width(1)) register_3 (.D(register_1_q[1]), .en(NEWBIT), .clk(CLK), .Q(register_1_q[2]), .clr(or_3_out));
  not not_3 (not_3_out, ENA);
  Register #(.width(1)) register_4 (.D(register_1_q[2]), .en(NEWBIT), .clk(CLK), .Q(register_1_q[3]), .clr(or_4_out));
  or or_3 (or_3_out, not_3_out, CLEAR);
  or or_4 (or_4_out, not_4_out, CLEAR);
  not not_4 (not_4_out, ENA);
  Register #(.width(1)) register_5 (.D(register_1_q[3]), .en(NEWBIT), .clk(CLK), .Q(register_1_q[4]), .clr(or_5_out));
  or or_5 (or_5_out, not_5_out, CLEAR);
  not not_5 (not_5_out, ENA);
  Counter #(.max('hd)) counter_1 (.count(NEWBIT), .carry(FULL), .clk(CLK), .clr(or_7_out));  // open: load, D, Q, up
  Register #(.width(1)) register_6 (.D(register_1_q[4]), .en(NEWBIT), .clk(CLK), .Q(register_1_q[5]), .clr(or_6_out));
  or or_6 (or_6_out, not_6_out, CLEAR);
  not not_6 (not_6_out, ENA);
  or or_7 (or_7_out, not_7_out, CLEAR);
  not not_7 (not_7_out, ENA);
  Register #(.width(1)) register_7 (.D(register_1_q[5]), .en(NEWBIT), .clk(CLK), .Q(register_1_q[6]), .clr(or_8_out));
  not not_8 (not_8_out, ENA);
  Register #(.width(1)) register_8 (.D(register_1_q[6]), .en(NEWBIT), .clk(CLK), .Q(register_1_q[7]), .clr(or_9_out));
  or or_8 (or_8_out, not_8_out, CLEAR);
  or or_9 (or_9_out, not_9_out, CLEAR);
  not not_9 (not_9_out, ENA);
  Register #(.width(1)) register_9 (.D(register_1_q[7]), .en(NEWBIT), .clk(CLK), .Q(register_1_q[8]), .clr(or_10_out));
  or or_10 (or_10_out, not_10_out, CLEAR);
  not not_10 (not_10_out, ENA);
  Register #(.width(1)) register_10 (.D(register_1_q[8]), .en(NEWBIT), .clk(CLK), .Q(register_1_q[9]), .clr(or_11_out));
  or or_11 (or_11_out, not_11_out, CLEAR);
  not not_11 (not_11_out, ENA);
  Register #(.width(1)) register_11 (
    .D(register_1_q[9]), .en(NEWBIT), .clk(CLK), .Q(register_1_q[10]), .clr(or_12_out));
  not not_12 (not_12_out, ENA);
  Register #(.width(1)) register_12 (
    .D(register_1_q[10]), .en(NEWBIT), .clk(CLK), .Q(register_1_q[11]), .clr(or_13_out));
  or or_12 (or_12_out, not_12_out, CLEAR);
  or or_13 (or_13_out, not_13_out, CLEAR);
  not not_13 (not_13_out, ENA);
  and and_1 (and_1_out, READ, FULL);
  Register #(.width(12)) register_13 (.D(register_1_q), .en(and_1_out), .clk(CLK), .Q(PARA_OUT));  // open: clr
endmodule

module VPWBSRO (
  input  [11:0] PARA_IN,
  input  LOAD,
  input  SHIFT,
  input  RELOAD,
  input  ENA,
  input  CLK,
  output SER_OUT,
  output EMPTY,
  output [3:0] BITSLEFT
);

  wire and_1_out, not_1_out, not_2_out, not_3_out, or_1_out, or_2_out, shift_register_1_q1,
       shift_register_1_q2, shift_register_1_q3, shift_register_1_q4, shift_register_1_q5,
       shift_register_1_q6, shift_register_1_q7, shift_register_1_q8, shift_register_1_q9,
       shift_register_1_q10, shift_register_1_q11;
  wire [11:0] multiplexer_1_out, register_1_q;

  and and_1 (and_1_out, EMPTY, LOAD);
  or or_1 (or_1_out, and_1_out, RELOAD);
  Counter #(.max('hd), .width(4)) counter_1 (
    .load(or_1_out), .D(4'b1101), .count(SHIFT), .Q(BITSLEFT), .up(1'b0), .clk(CLK), .clr(not_1_out));  // open: carry
  not not_1 (not_1_out, ENA);
  or or_2 (or_2_out, RELOAD, LOAD);
  Shift_Register #(.length(13)) shift_register_1 (
    .shift(SHIFT), .in(1'b0), .clk(CLK), .out(SER_OUT), .load(or_2_out), .clr(not_2_out), .d0(1'b1),
    .d1(multiplexer_1_out[0]), .q1(shift_register_1_q1), .d2(multiplexer_1_out[1]), .q2(shift_register_1_q2),
    .d3(multiplexer_1_out[2]), .q3(shift_register_1_q3), .d4(multiplexer_1_out[3]), .q4(shift_register_1_q4),
    .d5(multiplexer_1_out[4]), .q5(shift_register_1_q5), .d6(multiplexer_1_out[5]), .q6(shift_register_1_q6),
    .d7(multiplexer_1_out[6]), .q7(shift_register_1_q7), .d8(multiplexer_1_out[7]), .q8(shift_register_1_q8),
    .d9(multiplexer_1_out[8]), .q9(shift_register_1_q9), .d10(multiplexer_1_out[9]),
    .q10(shift_register_1_q10), .d11(multiplexer_1_out[10]), .q11(shift_register_1_q11),
    .d12(multiplexer_1_out[11]));  // open: q0, q12
  not not_2 (not_2_out, ENA);
  Multiplexer #(.width(12)) multiplexer_1 (.in0(PARA_IN), .in1(register_1_q), .out(multiplexer_1_out), .sel(RELOAD));
  nor nor_1 (EMPTY, shift_register_1_q1, shift_register_1_q2, shift_register_1_q3, shift_register_1_q4, shift_register_1_q5, shift_register_1_q6, shift_register_1_q7, shift_register_1_q8, shift_register_1_q9, shift_register_1_q10, shift_register_1_q11, SER_OUT);
  not not_3 (not_3_out, ENA);
  Register #(.width(12)) register_1 (.D(PARA_IN), .en(LOAD), .Q(register_1_q), .clk(CLK), .clr(not_3_out));
endmodule

module VPWBArbiter (
  input  EVENBIT,
  input  DOUT,
  input  DW,
  input  RX,
  input  ENA,
  input  CLK,
  output TX,
  output ARBL,
  output BITCMP
);

  wire and_1_out, and_2_out, and_3_out, and_4_out, and_6_out, and_7_out, and_8_out, and_9_out, and_11_out,
       BIT1, BIT2, IDLE, Long, not_1_out, not_2_out, not_3_out, not_4_out, not_5_out, not_6_out, not_7_out,
       not_8_out, not_9_out, register_1_q, ToBIT1, ToBIT2, ToIDLE, xor_1_out;

  not not_1 (not_1_out, ENA);
  not not_2 (not_2_out, DW);
  and and_1 (and_1_out, BIT2, not_2_out);
  and and_2 (and_2_out, BIT2, DW);
  not not_3 (not_3_out, ToIDLE);
  D_Flip_Flop d_ff_1 (.D(not_3_out), .clk(CLK), .Qn(IDLE), .reset(not_1_out));  // open: Q, preset
  D_Flip_Flop d_ff_2 (.D(ToBIT1), .clk(CLK), .Q(BIT1), .reset(not_1_out));  // open: Qn, preset
  D_Flip_Flop d_ff_3 (.D(ToBIT2), .clk(CLK), .Q(BIT2), .reset(not_1_out));  // open: Qn, preset
  // OR_Gate or_1 has open pins: in0=IDLE, in1=and_2_out, in2=and_1_out, out=open
  not not_4 (not_4_out, DW);
  not not_5 (not_5_out, DW);
  not not_6 (not_6_out, DW);
  xor xor_1 (xor_1_out, TX, RX);
  and and_3 (and_3_out, not_5_out, BIT1);
  and and_4 (and_4_out, not_6_out, BIT2);
  and and_5 (ToBIT2, BIT1, Long);
  and and_6 (and_6_out, IDLE, not_4_out);
  or or_2 (ToIDLE, and_6_out, and_3_out, and_4_out);
  not not_7 (not_7_out, IDLE);
  not not_8 (not_8_out, Long);
  not not_9 (not_9_out, Long);
  xor xor_2 (Long, EVENBIT, DOUT);
  and and_7 (and_7_out, BIT2, DW);
  and and_8 (and_8_out, BIT1, DW, not_9_out);
  and and_9 (and_9_out, IDLE, DW);
  Register #(.width(1)) register_1 (.D(EVENBIT), .en(1'b1), .clk(CLK), .Q(register_1_q));  // open: clr
  and and_10 (ARBL, not_7_out, xor_1_out);
  and and_11 (and_11_out, not_8_out, BIT1);
  or or_3 (ToBIT1, and_7_out, and_8_out, and_9_out);
  or or_4 (BITCMP, and_11_out, BIT2);
  Multiplexer multiplexer_1 (.in0(register_1_q), .in1(1'b0), .out(TX), .sel(IDLE));
endmodule

module VPWBObserver (
  input  RX,
  input  ENA,
  input  CLK,
  output IDLE,
  output DIN,
  output NEWBIT
);

  wire and_1_out, and_2_out, and_3_out, and_4_out, and_9_out, and_10_out, and_11_out, and_12_out, and_13_out,
       and_14_out, and_15_out, and_16_out, and_17_out, and_18_out, and_19_out, and_20_out, and_21_out,
       and_22_out, B0, B00, B1, B11, E0, E00, E1, not_1_out, not_2_out, not_3_out, not_4_out, not_5_out,
       not_6_out, not_7_out, not_8_out, not_9_out, not_10_out, not_11_out, not_12_out, not_13_out, ToB0,
       ToB00, ToB1, ToB11, ToE0, ToE00, ToE1, ToIDLE;

  not not_1 (not_1_out, ENA);
  and and_1 (and_1_out, E1, RX);
  and and_2 (and_2_out, RX, E00);
  and and_3 (and_3_out, RX, E0);
  and and_4 (and_4_out, RX, B11);
  or or_1 (ToE1, and_1_out, and_2_out, and_3_out, and_4_out);
  not not_2 (not_2_out, ToIDLE);
  not not_3 (not_3_out, RX);
  not not_4 (not_4_out, RX);
  not not_5 (not_5_out, RX);
  D_Flip_Flop d_ff_1 (.D(not_2_out), .clk(CLK), .Qn(IDLE), .reset(not_1_out));  // open: Q, preset
  D_Flip_Flop d_ff_2 (.D(ToB1), .clk(CLK), .Q(B1), .reset(not_1_out));  // open: Qn, preset
  D_Flip_Flop d_ff_3 (.D(ToB11), .clk(CLK), .Q(B11), .reset(not_1_out));  // open: Qn, preset
  D_Flip_Flop d_ff_4 (.D(ToB0), .clk(CLK), .Q(B0), .reset(not_1_out));  // open: Qn, preset
  D_Flip_Flop d_ff_5 (.D(ToB00), .clk(CLK), .Q(B00), .reset(not_1_out));  // open: Qn, preset
  D_Flip_Flop d_ff_6 (.D(ToE1), .clk(CLK), .Q(E1), .reset(not_1_out));  // open: Qn, preset
  D_Flip_Flop d_ff_7 (.D(ToE0), .clk(CLK), .Q(E0), .reset(not_1_out));  // open: Qn, preset
  and and_5 (ToE0, not_4_out, E1);
  and and_6 (ToE00, E0, not_5_out);
  D_Flip_Flop d_ff_8 (.D(ToE00), .clk(CLK), .Q(E00), .reset(not_1_out));  // open: Qn, preset
  and and_7 (ToB00, B0, not_3_out);
  and and_8 (ToB11, B1, RX);
  not not_6 (not_6_out, RX);
  not not_7 (not_7_out, RX);
  not not_8 (not_8_out, RX);
  not not_9 (not_9_out, RX);
  not not_10 (not_10_out, RX);
  and and_9 (and_9_out, B11, not_7_out);
  and and_10 (and_10_out, B0, RX);
  and and_11 (and_11_out, B00, RX);
  and and_12 (and_12_out, B1, not_6_out);
  and and_13 (and_13_out, B00, not_9_out);
  and and_14 (and_14_out, IDLE, not_11_out);
  not not_11 (not_11_out, RX);
  not not_12 (not_12_out, RX);
  not not_13 (not_13_out, RX);
  and and_15 (and_15_out, B0, RX);
  and and_16 (and_16_out, RX, B00);
  and and_17 (and_17_out, B1, not_10_out);
  and and_18 (and_18_out, B00, RX);
  or or_2 (DIN, and_11_out, and_12_out);
  and and_19 (and_19_out, not_8_out, E00);
  and and_20 (and_20_out, B1, not_12_out);
  and and_21 (and_21_out, not_13_out, B11);
  and and_22 (and_22_out, IDLE, RX);
  or or_3 (ToIDLE, and_19_out, and_13_out, and_14_out);
  or or_4 (ToB0, and_20_out, and_21_out);
  or or_5 (ToB1, and_22_out, and_15_out, and_16_out);
  or or_6 (NEWBIT, and_17_out, and_9_out, and_10_out, and_18_out);
endmodule

module observerDUY (
  input  RX,
  input  ENA,
  input  CLK,
  output IDLE,
  output DIN,
  output NEWBIT
);

  wire not_1_out, not_2_out, not_3_out, not_4_out, not_5_out, not_6_out, not_7_out, not_8_out, not_9_out,
       not_10_out, not_11_out, not_12_out, not_13_out, not_14_out, not_15_out, not_16_out, S0, S00, S1, S11;
  wire [2:0] register_1_q, register_2_q, register_3_q, register_4_q, register_5_q, rom_1_data;

  ROM #(.addrWidth(4), .dataWidth(3)) rom_1 (.addr({RX, register_1_q}), .data(rom_1_data));
  Register #(.width(3)) register_1 (.D(rom_1_data), .Q(register_1_q), .clk(CLK));  // open: en, clr
  not not_1 (not_1_out, register_1_q[2]);
  not not_2 (not_2_out, register_1_q[1]);
  and and_1 (IDLE, not_1_out, not_2_out, not_3_out);
  not not_3 (not_3_out, register_1_q[0]);
  Register #(.width(3)) register_2 (.D(register_1_q), .Q(register_2_q), .clk(CLK));  // open: en, clr
  Register #(.width(3)) register_3 (.D(register_1_q), .Q(register_3_q), .clk(CLK));  // open: en, clr
  Register #(.width(3)) register_4 (.D(register_1_q), .Q(register_4_q), .clk(CLK));  // open: en, clr
  Register #(.width(3)) register_5 (.D(register_1_q), .Q(register_5_q), .clk(CLK));  // open: en, clr
  not not_4 (not_4_out, register_2_q[0]);
  not not_5 (not_5_out, register_2_q[2]);
  and and_2 (S0, not_4_out, register_2_q[1], not_5_out, register_1_q[0], register_1_q[1], not_6_out);
  not not_6 (not_6_out, register_1_q[2]);
  not not_7 (not_7_out, register_3_q[2]);
  and and_3 (S00, register_3_q[0], register_3_q[1], not_7_out, register_1_q[0], not_8_out, not_9_out);
  not not_8 (not_8_out, register_1_q[1]);
  not not_9 (not_9_out, register_1_q[2]);
  not not_10 (not_10_out, register_4_q[0]);
  not not_11 (not_11_out, register_4_q[1]);
  and and_4 (S1, not_10_out, not_11_out, register_4_q[2], register_1_q[0], not_12_out, not_13_out);
  not not_12 (not_12_out, register_1_q[1]);
  not not_13 (not_13_out, register_1_q[2]);
  not not_14 (not_14_out, register_5_q[1]);
  not not_15 (not_15_out, register_5_q[2]);
  and and_5 (S11, register_5_q[0], not_14_out, not_15_out, register_1_q[0], register_1_q[1], not_16_out);
  not not_16 (not_16_out, register_1_q[2]);
  or or_1 (NEWBIT, S0, S00, S1, S11);
  or or_2 (DIN, S1, S11);

  // Notes on the sheet:
  //   contents of rom_1 (hex, n*v repeats v):
  //   0 3 3 4 0 6 7 0 1 2 5 1 1 5 5 5
endmodule

module BTXtest (
  input  CLK,
  input  [11:0] in_2,
  input  in_3,
  input  in_4,
  input  in_5
);

  wire pull_resistor_1_node, txrxd_1_din, vpwbmonitor_1_last_fe, vpwbrx_1_full, vpwbtx_1_full, vpwbtx_1_idle,
       vpwbtx_1_ser_out;
  wire [3:0] vpwbmonitor_1_last_addr;
  wire [7:0] vpwbmonitor_1_last_data;
  wire [11:0] vpwbrx_1_frame_out;
  wire [24:0] vpwbmonitor_1_out_4;
  wire [31:0] vpwbmonitor_1_out_3;

  // Probe on vpwbrx_1_frame_out
  // Probe on vpwbtx_1_full
  // Probe on vpwbtx_1_idle
  VPWBTX vpwbtx_1 (
    .FRAME_IN(in_2), .WRITE(in_3), .ENA(in_4), .CLK(CLK), .SER_IN(txrxd_1_din), .FULL(vpwbtx_1_full),
    .IDLE(vpwbtx_1_idle), .SER_OUT(vpwbtx_1_ser_out));
  VPWBRX vpwbrx_1 (
    .ENA(in_5), .CLK(CLK), .SER_IN(vpwbtx_1_ser_out), .FRAME_OUT(vpwbrx_1_frame_out), .FULL(vpwbrx_1_full));  // open: READ, CARE, ADDR, EMPTY
  Pull_Resistor #(.pull(1)) pull_resistor_1 (.node(pull_resistor_1_node));
  TXRXD txrxd_1 (.DOUT(vpwbtx_1_ser_out), .RXIN(pull_resistor_1_node), .DIN(txrxd_1_din), .TXOUT(pull_resistor_1_node));
  VPWBMonitor vpwbmonitor_1 (
    .RXIN(pull_resistor_1_node), .CLK(CLK), .LAST_FE(vpwbmonitor_1_last_fe),
    .LAST_ADDR(vpwbmonitor_1_last_addr), .LAST_DATA(vpwbmonitor_1_last_data), .out_3(vpwbmonitor_1_out_3),
    .out_4(vpwbmonitor_1_out_4));
  // Probe on vpwbmonitor_1_out_4
  // Probe on vpwbmonitor_1_last_fe
  // Probe on vpwbmonitor_1_last_addr
  // Probe on vpwbmonitor_1_last_data
  // Probe on vpwbmonitor_1_out_3

  // Notes on the sheet:
  //   in_2: initial=0x6af
endmodule
